// Logisim project Somador_Simples_2BITS.circ as structural Verilog: 1 circuit, main circuit SomadorSimles2Bits
module SomadorSimles2Bits (
  input  in_1,
  input  in_2,
  output out_3,
  output out_4
);

  and and_1 (out_4, in_1, in_2);
  xor xor_1 (out_3, in_1, in_2);
endmodule
