// Logisim project ULA.circ as structural Verilog: 3 circuits, main circuit main
// ULA
module main (
);

  wire [3:0] ula_1_s, undriven, undriven_2;

  ULA ula_1 (.A(undriven), .B(undriven_2), .S(ula_1_s));  // open: OpCode, OF
endmodule

module cellULA (
  input  a,
  input  b,
  input  [1:0] op,
  input  cin,
  output s,
  output cout
);

  wire adder_1_cout, adder_1_out, and_1_out, or_1_out;

  and and_1 (and_1_out, a, b);
  or or_1 (or_1_out, a, b);
  // XOR_Gate xor_1 has open pins: in0=a, in1=b, out=open
  // NOR_Gate nor_1 has open pins: in0=a, in1=b, out=open
  Adder #(.width(1)) adder_1 (.out(adder_1_out), .cin(cin), .cout(adder_1_cout));  // open: a, b
endmodule

module ULA (
  input  [3:0] A,
  input  [3:0] B,
  input  [1:0] OpCode,
  output [3:0] S,
  output OF
);

  wire cellula_1_p6, cellula_2_p7, cellula_3_p6;

  // cellULA cellula_1: pin names not known; wires that end beside it: A[0], B[0], 1'b0, OpCode, S[0], cellula_1_p6
  // cellULA cellula_2: pin names not known; wires that end beside it: A[1], B[1], cellula_1_p6, OpCode, OpCode, S[1], cellula_2_p7
  // cellULA cellula_3: pin names not known; wires that end beside it: A[2], B[2], cellula_2_p7, OpCode, S[2], cellula_3_p6
  // cellULA cellula_4: pin names not known; wires that end beside it: A[3], B[3], cellula_3_p6, OpCode, S[3], OF
endmodule
