// Logisim project ULA_Bráulio.circ as structural Verilog: 3 circuits, main circuit main
// ULA
module main (
);

  wire [3:0] ula_1_s, undriven, undriven_2;

  ULA ula_1 (.A(undriven), .B(undriven_2), .S(ula_1_s));  // open: OpCode, OF
endmodule

module cellULA (
  input  a,
  input  b,
  input  cin,
  input  [1:0] op,
  output s,
  output cout
);

  wire adder_1_out, and_1_out, or_1_out;

  and and_1 (and_1_out, a, b);
  or or_1 (or_1_out, a, b);
  Adder #(.width(1)) adder_1 (.a(a), .b(b), .out(adder_1_out), .cin(cin), .cout(cout));
  Multiplexer #(.select(2), .enable("false")) multiplexer_1 (
    .in0(and_1_out), .in1(or_1_out), .in2(adder_1_out), .out(s), .sel(op));  // open: in3
endmodule

module ULA (
  input  [3:0] A,
  input  [3:0] B,
  input  [1:0] OpCode,
  output [3:0] S,
  output OF
);

  wire cellula_1_cout, cellula_2_cout, cellula_3_cout;

  cellULA cellula_1 (.a(A[0]), .b(B[0]), .cin(1'b0), .op(OpCode), .s(S[0]), .cout(cellula_1_cout));
  cellULA cellula_2 (.a(A[1]), .b(B[1]), .cin(cellula_1_cout), .op(OpCode), .s(S[1]), .cout(cellula_2_cout));
  cellULA cellula_3 (.a(A[2]), .b(B[2]), .cin(cellula_2_cout), .op(OpCode), .s(S[2]), .cout(cellula_3_cout));
  cellULA cellula_4 (.a(A[3]), .b(B[3]), .cin(cellula_3_cout), .op(OpCode), .s(S[3]), .cout(OF));
endmodule
