// Logisim project ULA_David.circ as structural Verilog
module BCD8421_para_Gray (
  input  A,
  input  B,
  input  C,
  input  D,
  output S0,
  output S1,
  output S2,
  output S3
);

  or A___B (S1, A, B);
  xor B_____C (S2, B, C);
  xor C_____D (S3, C, D);

  assign S0 = A;
endmodule

// +
module CircuitoSomador (
  input  A,
  input  B,
  input  CIN,
  output S,
  output COUT
);

  wire and_1_out, or_1_out, xnor_1_out, xor_1_out;

  xor xor_1 (xor_1_out, B, A);
  xnor xnor_1 (xnor_1_out, B, A);
  and and_1 (and_1_out, B, A);
  or or_1 (or_1_out, B, A);
  Multiplexer multiplexer_1 (.in0(xor_1_out), .in1(xnor_1_out), .out(S), .sel(CIN));  // open: en
  Multiplexer multiplexer_2 (.in0(and_1_out), .in1(or_1_out), .out(COUT), .sel(CIN));  // open: en

  // Notes on the sheet:
  //   Circuito Somador com MUX 2x1
endmodule

module CircuitoSomadorMUX (
  input  [2:0] A_B_CIN,
  output S,
  output COUT
);

  Multiplexer #(.select(3)) multiplexer_1 (
    .in0(1'b0), .in1(1'b1), .in2(1'b1), .in3(1'b0), .in4(1'b1), .in5(1'b0), .in6(1'b0), .in7(1'b1), .out(S),
    .sel(A_B_CIN));  // open: en
  Multiplexer #(.select(3)) multiplexer_2 (
    .in0(1'b0), .in1(1'b0), .in2(1'b0), .in3(1'b1), .in4(1'b0), .in5(1'b1), .in6(1'b1), .in7(1'b1),
    .out(COUT), .sel(A_B_CIN));  // open: en

  // Notes on the sheet:
  //   Circuito Somador com MUX 8x1
endmodule

// -
module CircuitoSubtrator (
  input  A,
  input  B,
  input  CIN,
  output S,
  output COUT
);

  wire not_1_out, not_2_out, not_3_out, or_1_out, or_2_out, xnor_1_out, xor_1_out;

  not not_1 (not_1_out, B);
  not not_2 (not_2_out, A);
  xor xor_1 (xor_1_out, B, A);
  Multiplexer multiplexer_1 (.in0(xor_1_out), .in1(xnor_1_out), .out(S), .sel(CIN));  // open: en
  xnor xnor_1 (xnor_1_out, B, A);
  or or_1 (or_1_out, not_1_out, A);
  not not_3 (not_3_out, or_1_out);
  or or_2 (or_2_out, B, not_2_out);
  Multiplexer multiplexer_2 (.in0(not_3_out), .in1(or_2_out), .out(COUT), .sel(CIN));  // open: en

  // Notes on the sheet:
  //   Circuito Subtrator com MUX 2x1
endmodule

module CircuitoSubtratorMUX (
  input  [2:0] A_B_CIN,
  output S,
  output COUT
);

  Multiplexer #(.select(3)) multiplexer_1 (
    .in0(1'b0), .in1(1'b1), .in2(1'b1), .in3(1'b0), .in4(1'b1), .in5(1'b0), .in6(1'b0), .in7(1'b1), .out(S),
    .sel(A_B_CIN));  // open: en
  Multiplexer #(.select(3)) multiplexer_2 (
    .in0(1'b0), .in1(1'b1), .in2(1'b0), .in3(1'b0), .in4(1'b1), .in5(1'b1), .in6(1'b0), .in7(1'b1),
    .out(COUT), .sel(A_B_CIN));  // open: en

  // Notes on the sheet:
  //   Circuito Subtrator com MUX 8x1
endmodule

module ULA (
  input  A,
  input  B,
  input  [1:0] in_3,
  input  CIN,
  output out_5,
  output COUT,
  output COUT_2
);

  wire AND_out, circuitosomador_1_s, circuitosubtrator_1_s, OR_out;

  and AND (AND_out, A, B);
  or OR (OR_out, A, B);
  CircuitoSomador circuitosomador_1 (.CIN(CIN), .A(A), .B(B), .S(circuitosomador_1_s), .COUT(COUT));
  CircuitoSubtrator circuitosubtrator_1 (.CIN(CIN), .A(A), .B(B), .S(circuitosubtrator_1_s), .COUT(COUT_2));
  Multiplexer #(.select(2), .enable("false")) multiplexer_1 (
    .in0(AND_out), .in1(OR_out), .in2(circuitosomador_1_s), .in3(circuitosubtrator_1_s), .out(out_5),
    .sel(in_3));
endmodule
