// Logisim project contadores.circ as structural Verilog: 4 circuits, main circuit main
module main (
  output out_1
);

  wire clock_1_out;
  wire [3:0] contador0_59_1_dezena, contador0_59_1_unidade, contador0_59_2_dezena, contador0_59_2_unidade;

  Hex_Digit_Display hex_digit_display_1 (.value(contador0_59_1_dezena));  // open: dp
  Clock clock_1 (.out(clock_1_out));
  contador0_59 contador0_59_1 (.clk(out_1), .dezena(contador0_59_1_dezena), .unidade(contador0_59_1_unidade));
  Hex_Digit_Display hex_digit_display_2 (.value(contador0_59_1_unidade));  // open: dp
  contador0_59 contador0_59_2 (.clk(clock_1_out), .dezena(contador0_59_2_dezena), .unidade(contador0_59_2_unidade));
  Hex_Digit_Display hex_digit_display_3 (.value(contador0_59_2_dezena));  // open: dp
  Hex_Digit_Display hex_digit_display_4 (.value(contador0_59_2_unidade));  // open: dp
  and and_1 (out_1, ~contador0_59_2_dezena[0], ~contador0_59_2_dezena[1], ~contador0_59_2_dezena[2], ~contador0_59_2_dezena[3]);  // AND_Gate
endmodule

module contador0_9 (
  input  clk,
  output [3:0] Estado
);

  wire and_1_out, and_2_out, d_ff_4_qn, multiplexer_1_out, multiplexer_2_out, or_1_out;

  or or_1 (or_1_out, and_1_out, and_2_out);
  D_Flip_Flop d_ff_1 (.clk(clk), .D(or_1_out), .Q(Estado[3]));  // open: Qn, preset, en, reset
  and and_1 (and_1_out, Estado[3], ~Estado[0], ~Estado[1], ~Estado[2]);  // AND_Gate
  and and_2 (and_2_out, ~Estado[3], Estado[0], Estado[1], Estado[2]);  // AND_Gate
  D_Flip_Flop d_ff_2 (.clk(clk), .D(multiplexer_1_out), .Q(Estado[2]));  // open: Qn, preset, en, reset
  D_Flip_Flop d_ff_3 (.clk(clk), .D(multiplexer_2_out), .Q(Estado[1]));  // open: Qn, preset, en, reset
  Hex_Digit_Display hex_digit_display_1 (.value(Estado));  // open: dp
  D_Flip_Flop d_ff_4 (.clk(clk), .D(d_ff_4_qn), .Q(Estado[0]), .Qn(d_ff_4_qn));  // open: preset, en, reset
  Multiplexer #(.select(4), .enable("false")) multiplexer_1 (
    .in0(1'b0), .in1(1'b0), .in2(1'b0), .in3(1'b1), .in4(1'b1), .in5(1'b1), .in6(1'b1), .in7(1'b0),
    .in8(1'b0), .in9(1'b0), .in10(1'b0), .in11(1'b0), .in12(1'b0), .in13(1'b0), .in14(1'b0), .in15(1'b0),
    .out(multiplexer_1_out), .sel(Estado));
  Multiplexer #(.select(4), .enable("false")) multiplexer_2 (
    .in0(1'b0), .in1(1'b1), .in2(1'b1), .in3(1'b0), .in4(1'b0), .in5(1'b1), .in6(1'b1), .in7(1'b0),
    .in8(1'b0), .in9(1'b0), .out(multiplexer_2_out), .sel(Estado));  // open: in10, in11, in12, in13, in14, in15
endmodule

module contador0_5 (
  input  clk,
  output [3:0] Estado
);

  wire d_ff_3_qn, multiplexer_1_out, multiplexer_2_out;

  D_Flip_Flop d_ff_1 (.clk(clk), .D(multiplexer_1_out), .Q(Estado[2]));  // open: Qn, preset, en, reset
  D_Flip_Flop d_ff_2 (.clk(clk), .D(multiplexer_2_out), .Q(Estado[1]));  // open: Qn, preset, en, reset
  Hex_Digit_Display hex_digit_display_1 (.value({1'b0, Estado[2:0]}));  // open: dp
  D_Flip_Flop d_ff_3 (.clk(clk), .D(d_ff_3_qn), .Q(Estado[0]), .Qn(d_ff_3_qn));  // open: preset, en, reset
  Multiplexer #(.select(3), .enable("false")) multiplexer_1 (
    .in0(1'b0), .in1(1'b0), .in2(1'b0), .in3(1'b1), .in4(1'b1), .in5(1'b0), .in6(1'b0), .in7(1'b0),
    .out(multiplexer_1_out), .sel(Estado[2:0]));
  Multiplexer #(.select(3), .enable("false")) multiplexer_2 (
    .in0(1'b0), .in1(1'b1), .in2(1'b1), .in3(1'b0), .in4(1'b0), .in5(1'b0), .in6(1'b0), .in7(1'b0),
    .out(multiplexer_2_out), .sel(Estado[2:0]));

  assign Estado[3] = 1'b0;
endmodule

module contador0_59 (
  input  clk,
  output [3:0] dezena,
  output [3:0] unidade
);

  wire and_1_out;

  contador0_5 contador0_5_1 (.clk(and_1_out), .Estado(dezena));
  Hex_Digit_Display hex_digit_display_1 (.value(dezena));  // open: dp
  contador0_9 contador0_9_1 (.clk(clk), .Estado(unidade));
  Hex_Digit_Display hex_digit_display_2 (.value(unidade));  // open: dp
  and and_1 (and_1_out, ~unidade[0], ~unidade[1], ~unidade[2], ~unidade[3]);  // AND_Gate
endmodule
