// Logisim project tuamae.circ as structural Verilog
module REGISTRADOR (
  input  [31:0] dIN,
  input  clk,
  input  clr,
  output [31:0] dOUT
);

  D_Flip_Flop d_ff_1 (.clk(clk), .D(dIN[31]), .Q(dOUT[31]), .reset(clr));  // open: Qn, preset, en
  D_Flip_Flop d_ff_2 (.clk(clk), .D(dIN[30]), .Q(dOUT[30]), .reset(clr));  // open: Qn, preset, en
  D_Flip_Flop d_ff_3 (.clk(clk), .D(dIN[29]), .Q(dOUT[29]), .reset(clr));  // open: Qn, preset, en
  D_Flip_Flop d_ff_4 (.clk(clk), .D(dIN[28]), .Q(dOUT[28]), .reset(clr));  // open: Qn, preset, en
  D_Flip_Flop d_ff_5 (.clk(clk), .D(dIN[27]), .Q(dOUT[27]), .reset(clr));  // open: Qn, preset, en
  D_Flip_Flop d_ff_6 (.clk(clk), .D(dIN[26]), .Q(dOUT[26]), .reset(clr));  // open: Qn, preset, en
  D_Flip_Flop d_ff_7 (.clk(clk), .D(dIN[25]), .Q(dOUT[25]), .reset(clr));  // open: Qn, preset, en
  D_Flip_Flop d_ff_8 (.clk(clk), .D(dIN[24]), .Q(dOUT[24]), .reset(clr));  // open: Qn, preset, en
  D_Flip_Flop d_ff_9 (.clk(clk), .D(dIN[23]), .Q(dOUT[23]), .reset(clr));  // open: Qn, preset, en
  D_Flip_Flop d_ff_10 (.clk(clk), .D(dIN[22]), .Q(dOUT[22]), .reset(clr));  // open: Qn, preset, en
  D_Flip_Flop d_ff_11 (.clk(clk), .D(dIN[21]), .Q(dOUT[21]), .reset(clr));  // open: Qn, preset, en
  D_Flip_Flop d_ff_12 (.clk(clk), .D(dIN[20]), .Q(dOUT[20]), .reset(clr));  // open: Qn, preset, en
  D_Flip_Flop d_ff_13 (.clk(clk), .D(dIN[19]), .Q(dOUT[19]), .reset(clr));  // open: Qn, preset, en
  D_Flip_Flop d_ff_14 (.clk(clk), .D(dIN[18]), .Q(dOUT[18]), .reset(clr));  // open: Qn, preset, en
  D_Flip_Flop d_ff_15 (.clk(clk), .D(dIN[17]), .Q(dOUT[17]), .reset(clr));  // open: Qn, preset, en
  D_Flip_Flop d_ff_16 (.clk(clk), .D(dIN[16]), .Q(dOUT[16]), .reset(clr));  // open: Qn, preset, en
  D_Flip_Flop d_ff_17 (.clk(clk), .D(dIN[15]), .Q(dOUT[15]), .reset(clr));  // open: Qn, preset, en
  D_Flip_Flop d_ff_18 (.clk(clk), .D(dIN[14]), .Q(dOUT[14]), .reset(clr));  // open: Qn, preset, en
  D_Flip_Flop d_ff_19 (.clk(clk), .D(dIN[13]), .Q(dOUT[13]), .reset(clr));  // open: Qn, preset, en
  D_Flip_Flop d_ff_20 (.clk(clk), .D(dIN[12]), .Q(dOUT[12]), .reset(clr));  // open: Qn, preset, en
  D_Flip_Flop d_ff_21 (.clk(clk), .D(dIN[11]), .Q(dOUT[11]), .reset(clr));  // open: Qn, preset, en
  D_Flip_Flop d_ff_22 (.clk(clk), .D(dIN[10]), .Q(dOUT[10]), .reset(clr));  // open: Qn, preset, en
  D_Flip_Flop d_ff_23 (.clk(clk), .D(dIN[9]), .Q(dOUT[9]), .reset(clr));  // open: Qn, preset, en
  D_Flip_Flop d_ff_24 (.clk(clk), .D(dIN[8]), .Q(dOUT[8]), .reset(clr));  // open: Qn, preset, en
  D_Flip_Flop d_ff_25 (.clk(clk), .D(dIN[7]), .Q(dOUT[7]), .reset(clr));  // open: Qn, preset, en
  D_Flip_Flop d_ff_26 (.clk(clk), .D(dIN[6]), .Q(dOUT[6]), .reset(clr));  // open: Qn, preset, en
  D_Flip_Flop d_ff_27 (.clk(clk), .D(dIN[5]), .Q(dOUT[5]), .reset(clr));  // open: Qn, preset, en
  D_Flip_Flop d_ff_28 (.clk(clk), .D(dIN[4]), .Q(dOUT[4]), .reset(clr));  // open: Qn, preset, en
  D_Flip_Flop d_ff_29 (.clk(clk), .D(dIN[3]), .Q(dOUT[3]), .reset(clr));  // open: Qn, preset, en
  D_Flip_Flop d_ff_30 (.clk(clk), .D(dIN[2]), .Q(dOUT[2]), .reset(clr));  // open: Qn, preset, en
  D_Flip_Flop d_ff_31 (.clk(clk), .D(dIN[1]), .Q(dOUT[1]), .reset(clr));  // open: Qn, preset, en
  D_Flip_Flop d_ff_32 (.clk(clk), .D(dIN[0]), .Q(dOUT[0]), .reset(clr));  // open: Qn, preset, en
endmodule

module BANCO_DE_REGISTRADORES (
  input  [31:0] ENTRADA,
  input  CLK,
  input  [4:0] SELETOR_DE_ENTRADA,
  input  [4:0] \SELETOR_DE_SAÍDA___A ,
  input  [4:0] \SELETOR_DE_SAÍDA___B ,
  output [31:0] \SAÍDA ,
  output [31:0] \SAÍDA_2 
);

  wire demultiplexer_1_out0, demultiplexer_1_out1, demultiplexer_1_out2, demultiplexer_1_out3,
       demultiplexer_1_out4, demultiplexer_1_out5, demultiplexer_1_out6, demultiplexer_1_out7,
       demultiplexer_1_out8, demultiplexer_1_out9, demultiplexer_1_out10, demultiplexer_1_out11,
       demultiplexer_1_out12, demultiplexer_1_out13, demultiplexer_1_out14, demultiplexer_1_out15,
       demultiplexer_1_out16, demultiplexer_1_out17, demultiplexer_1_out18, demultiplexer_1_out19,
       demultiplexer_1_out20, demultiplexer_1_out21, demultiplexer_1_out22, demultiplexer_1_out23,
       demultiplexer_1_out24, demultiplexer_1_out25, demultiplexer_1_out26, demultiplexer_1_out27,
       demultiplexer_1_out28, demultiplexer_1_out29, demultiplexer_1_out30, demultiplexer_1_out31;
  wire [31:0] registrador_1_dout, registrador_2_dout, registrador_3_dout, registrador_4_dout,
       registrador_5_dout, registrador_6_dout, registrador_7_dout, registrador_8_dout, registrador_9_dout,
       registrador_10_dout, registrador_11_dout, registrador_12_dout, registrador_13_dout,
       registrador_14_dout, registrador_15_dout, registrador_16_dout, registrador_17_dout,
       registrador_18_dout, registrador_19_dout, registrador_20_dout, registrador_21_dout,
       registrador_22_dout, registrador_23_dout, registrador_24_dout, registrador_25_dout,
       registrador_26_dout, registrador_27_dout, registrador_28_dout, registrador_29_dout,
       registrador_30_dout, registrador_31_dout, registrador_32_dout;

  Demultiplexer #(.select(5), .enable("false")) demultiplexer_1 (
    .out0(demultiplexer_1_out0), .out1(demultiplexer_1_out1), .out2(demultiplexer_1_out2),
    .out3(demultiplexer_1_out3), .out4(demultiplexer_1_out4), .out5(demultiplexer_1_out5),
    .out6(demultiplexer_1_out6), .out7(demultiplexer_1_out7), .out8(demultiplexer_1_out8),
    .out9(demultiplexer_1_out9), .out10(demultiplexer_1_out10), .out11(demultiplexer_1_out11),
    .out12(demultiplexer_1_out12), .out13(demultiplexer_1_out13), .out14(demultiplexer_1_out14),
    .out15(demultiplexer_1_out15), .out16(demultiplexer_1_out16), .out17(demultiplexer_1_out17),
    .out18(demultiplexer_1_out18), .out19(demultiplexer_1_out19), .out20(demultiplexer_1_out20),
    .out21(demultiplexer_1_out21), .out22(demultiplexer_1_out22), .out23(demultiplexer_1_out23),
    .out24(demultiplexer_1_out24), .out25(demultiplexer_1_out25), .out26(demultiplexer_1_out26),
    .out27(demultiplexer_1_out27), .out28(demultiplexer_1_out28), .out29(demultiplexer_1_out29),
    .out30(demultiplexer_1_out30), .out31(demultiplexer_1_out31), .in(CLK), .sel(SELETOR_DE_ENTRADA));
  REGISTRADOR registrador_1 (.clk(demultiplexer_1_out0), .dIN(ENTRADA), .dOUT(registrador_1_dout));  // open: clr
  REGISTRADOR registrador_2 (.clk(demultiplexer_1_out1), .dIN(ENTRADA), .dOUT(registrador_2_dout));  // open: clr
  REGISTRADOR registrador_3 (.clk(demultiplexer_1_out2), .dIN(ENTRADA), .dOUT(registrador_3_dout));  // open: clr
  REGISTRADOR registrador_4 (.clk(demultiplexer_1_out3), .dIN(ENTRADA), .dOUT(registrador_4_dout));  // open: clr
  REGISTRADOR registrador_5 (.clk(demultiplexer_1_out4), .dIN(ENTRADA), .dOUT(registrador_5_dout));  // open: clr
  REGISTRADOR registrador_6 (.clk(demultiplexer_1_out5), .dIN(ENTRADA), .dOUT(registrador_6_dout));  // open: clr
  REGISTRADOR registrador_7 (.clk(demultiplexer_1_out6), .dIN(ENTRADA), .dOUT(registrador_7_dout));  // open: clr
  REGISTRADOR registrador_8 (.clk(demultiplexer_1_out7), .dIN(ENTRADA), .dOUT(registrador_8_dout));  // open: clr
  REGISTRADOR registrador_9 (.clk(demultiplexer_1_out8), .dIN(ENTRADA), .dOUT(registrador_9_dout));  // open: clr
  REGISTRADOR registrador_10 (.clk(demultiplexer_1_out9), .dIN(ENTRADA), .dOUT(registrador_10_dout));  // open: clr
  REGISTRADOR registrador_11 (.clk(demultiplexer_1_out10), .dIN(ENTRADA), .dOUT(registrador_11_dout));  // open: clr
  REGISTRADOR registrador_12 (.clk(demultiplexer_1_out11), .dIN(ENTRADA), .dOUT(registrador_12_dout));  // open: clr
  REGISTRADOR registrador_13 (.clk(demultiplexer_1_out12), .dIN(ENTRADA), .dOUT(registrador_13_dout));  // open: clr
  REGISTRADOR registrador_14 (.clk(demultiplexer_1_out13), .dIN(ENTRADA), .dOUT(registrador_14_dout));  // open: clr
  REGISTRADOR registrador_15 (.clk(demultiplexer_1_out14), .dIN(ENTRADA), .dOUT(registrador_15_dout));  // open: clr
  REGISTRADOR registrador_16 (.clk(demultiplexer_1_out15), .dIN(ENTRADA), .dOUT(registrador_16_dout));  // open: clr
  REGISTRADOR registrador_17 (.clk(demultiplexer_1_out16), .dIN(ENTRADA), .dOUT(registrador_17_dout));  // open: clr
  REGISTRADOR registrador_18 (.clk(demultiplexer_1_out17), .dIN(ENTRADA), .dOUT(registrador_18_dout));  // open: clr
  REGISTRADOR registrador_19 (.clk(demultiplexer_1_out18), .dIN(ENTRADA), .dOUT(registrador_19_dout));  // open: clr
  REGISTRADOR registrador_20 (.clk(demultiplexer_1_out19), .dIN(ENTRADA), .dOUT(registrador_20_dout));  // open: clr
  REGISTRADOR registrador_21 (.clk(demultiplexer_1_out20), .dIN(ENTRADA), .dOUT(registrador_21_dout));  // open: clr
  REGISTRADOR registrador_22 (.clk(demultiplexer_1_out21), .dIN(ENTRADA), .dOUT(registrador_22_dout));  // open: clr
  REGISTRADOR registrador_23 (.clk(demultiplexer_1_out22), .dIN(ENTRADA), .dOUT(registrador_23_dout));  // open: clr
  REGISTRADOR registrador_24 (.clk(demultiplexer_1_out23), .dIN(ENTRADA), .dOUT(registrador_24_dout));  // open: clr
  REGISTRADOR registrador_25 (.clk(demultiplexer_1_out24), .dIN(ENTRADA), .dOUT(registrador_25_dout));  // open: clr
  REGISTRADOR registrador_26 (.clk(demultiplexer_1_out25), .dIN(ENTRADA), .dOUT(registrador_26_dout));  // open: clr
  REGISTRADOR registrador_27 (.clk(demultiplexer_1_out26), .dIN(ENTRADA), .dOUT(registrador_27_dout));  // open: clr
  REGISTRADOR registrador_28 (.clk(demultiplexer_1_out27), .dIN(ENTRADA), .dOUT(registrador_28_dout));  // open: clr
  REGISTRADOR registrador_29 (.clk(demultiplexer_1_out28), .dIN(ENTRADA), .dOUT(registrador_29_dout));  // open: clr
  REGISTRADOR registrador_30 (.clk(demultiplexer_1_out29), .dIN(ENTRADA), .dOUT(registrador_30_dout));  // open: clr
  REGISTRADOR registrador_31 (.clk(demultiplexer_1_out30), .dIN(ENTRADA), .dOUT(registrador_31_dout));  // open: clr
  REGISTRADOR registrador_32 (.clk(demultiplexer_1_out31), .dIN(ENTRADA), .dOUT(registrador_32_dout));  // open: clr
  Multiplexer #(.select(5), .width(32), .enable("false")) multiplexer_1 (
    .in0(registrador_1_dout), .in1(registrador_2_dout), .in2(registrador_3_dout), .in3(registrador_4_dout),
    .in4(registrador_5_dout), .in5(registrador_6_dout), .in6(registrador_7_dout), .in7(registrador_8_dout),
    .in8(registrador_9_dout), .in9(registrador_10_dout), .in10(registrador_11_dout),
    .in11(registrador_12_dout), .in12(registrador_13_dout), .in13(registrador_14_dout),
    .in14(registrador_15_dout), .in15(registrador_16_dout), .in16(registrador_17_dout),
    .in17(registrador_18_dout), .in18(registrador_19_dout), .in19(registrador_20_dout),
    .in20(registrador_21_dout), .in21(registrador_22_dout), .in22(registrador_23_dout),
    .in23(registrador_24_dout), .in24(registrador_25_dout), .in25(registrador_26_dout),
    .in26(registrador_27_dout), .in27(registrador_28_dout), .in28(registrador_29_dout),
    .in29(registrador_30_dout), .in30(registrador_31_dout), .in31(registrador_32_dout), .out(\SAÍDA ),
    .sel(\SELETOR_DE_SAÍDA___A ));
  Multiplexer #(.select(5), .width(32), .enable("false")) multiplexer_2 (
    .in0(registrador_1_dout), .in1(registrador_2_dout), .in2(registrador_3_dout), .in3(registrador_4_dout),
    .in4(registrador_5_dout), .in5(registrador_6_dout), .in6(registrador_7_dout), .in7(registrador_8_dout),
    .in8(registrador_9_dout), .in9(registrador_10_dout), .in10(registrador_11_dout),
    .in11(registrador_12_dout), .in12(registrador_13_dout), .in13(registrador_14_dout),
    .in14(registrador_15_dout), .in15(registrador_16_dout), .in16(registrador_17_dout),
    .in17(registrador_18_dout), .in18(registrador_19_dout), .in19(registrador_20_dout),
    .in20(registrador_21_dout), .in21(registrador_22_dout), .in22(registrador_23_dout),
    .in23(registrador_24_dout), .in24(registrador_25_dout), .in25(registrador_26_dout),
    .in26(registrador_27_dout), .in27(registrador_28_dout), .in28(registrador_29_dout),
    .in29(registrador_30_dout), .in30(registrador_31_dout), .in31(registrador_32_dout), .out(\SAÍDA_2 ),
    .sel(\SELETOR_DE_SAÍDA___B ));
endmodule

module celULA (
  input  A,
  input  B,
  input  cin,
  input  ESQUERDA,
  input  DIREITA,
  input  DIREITA_A,
  input  COMPARADOR,
  input  [4:0] \OPERAÇÃO ,
  output \SAÍDA ,
  output cout,
  output SET
);

  wire adder_1_cout, adder_1_out, and_2_out, AND_out, multiplexer_2_out, multiplexer_3_out, NAND_out,
       NOR_out, OR_out, subtractor_1_out, XNOR_out, XOR_out;

  and AND (AND_out, A, B);
  or OR (OR_out, A, B);
  xor XOR (XOR_out, A, B);
  xnor XNOR (XNOR_out, A, B);
  nand NAND (NAND_out, A, B);
  nor NOR (NOR_out, A, B);
  Adder #(.width(1)) adder_1 (.a(A), .b(B), .out(adder_1_out), .cin(cin), .cout(adder_1_cout));
  Subtractor #(.width(1)) subtractor_1 (.a(A), .b(B), .out(subtractor_1_out), .bin(cin), .bout(SET));
  and and_2 (and_2_out, \OPERAÇÃO [0], \OPERAÇÃO [1], \OPERAÇÃO [2], ~\OPERAÇÃO [3], ~\OPERAÇÃO [4]);  // AND_Gate
  Multiplexer #(.enable("false")) multiplexer_1 (.in0(adder_1_cout), .in1(SET), .out(cout), .sel(and_2_out));
  Multiplexer #(.select(5), .enable("false")) multiplexer_2 (
    .in0(AND_out), .in1(OR_out), .in2(XOR_out), .in3(XNOR_out), .in4(NAND_out), .in5(NOR_out),
    .in6(adder_1_out), .in7(subtractor_1_out), .in8(ESQUERDA), .in9(DIREITA), .in10(DIREITA_A),
    .in11(COMPARADOR), .out(multiplexer_2_out), .sel(\OPERAÇÃO ));  // open: in12, in13, in14, in15, in16, in17, in18, in19, in20, in21, in22, in23, in24, in25, in26, in27, in28, in29, in30, in31
  Multiplexer #(.select(5), .enable("false")) multiplexer_3 (
    .out(multiplexer_3_out), .sel(\OPERAÇÃO ));  // open: in0, in1, in2, in3, in4, in5, in6, in7, in8, in9, in10, in11, in12, in13, in14, in15, in16, in17, in18, in19, in20, in21, in22, in23, in24, in25, in26, in27, in28, in29, in30, in31
  Multiplexer #(.enable("false")) multiplexer_4 (
    .in0(multiplexer_2_out), .in1(multiplexer_3_out), .out(\SAÍDA ), .sel(1'b0));

  // Notes on the sheet:
  //   00000
  //   00001
  //   00010
  //   00011
  //   00100
  //   00101
  //   00110
  //   00111
  //   01000
  //   01001
  //   01010
  //   01011
endmodule

module ULA (
  input  [31:0] A,
  input  [31:0] B,
  input  [4:0] in_3,
  input  [31:0] in_4,
  output OVERFLOW,
  output out_6
);

  wire celula_1_cout, celula_2_cout, celula_3_cout, celula_4_cout, celula_5_cout, celula_6_cout,
       celula_7_cout, celula_8_cout, celula_9_cout, celula_10_cout, celula_11_cout, celula_12_cout,
       celula_13_cout, celula_14_cout, celula_15_cout, celula_16_cout, celula_17_cout, celula_18_cout,
       celula_19_cout, celula_20_cout, celula_21_cout, celula_22_cout, celula_23_cout, celula_24_cout,
       celula_25_cout, celula_26_cout, celula_27_cout, celula_28_cout, celula_29_cout, celula_30_cout,
       celula_31_cout, celula_32_cout;

  OVERFLOW overflow_1 (
    .OP(in_3), .E1(A[31]), .E2(A[31]), .\SAÍDA (A[31]), .OVERFLOW(OVERFLOW));  // open: in_4, in_5, in_6
  celULA celula_1 (
    .cout(celula_1_cout), .ESQUERDA(A[30]), .\OPERAÇÃO (in_3), .A(A[31]), .B(B[31]), .cin(1'b0),
    .\SAÍDA (in_4[31]), .DIREITA(1'b0));  // open: SET, DIREITA_A, COMPARADOR
  celULA celula_2 (
    .cout(celula_2_cout), .ESQUERDA(A[29]), .\OPERAÇÃO (in_3), .A(A[30]), .B(B[30]), .cin(celula_1_cout),
    .\SAÍDA (in_4[30]), .DIREITA(A[31]));  // open: SET, DIREITA_A, COMPARADOR
  celULA celula_3 (
    .cout(celula_3_cout), .ESQUERDA(A[28]), .\OPERAÇÃO (in_3), .A(A[29]), .B(B[29]), .cin(celula_2_cout),
    .\SAÍDA (in_4[29]), .DIREITA(A[30]));  // open: SET, DIREITA_A, COMPARADOR
  celULA celula_4 (
    .cout(celula_4_cout), .ESQUERDA(A[27]), .\OPERAÇÃO (in_3), .A(A[28]), .B(B[28]), .cin(celula_3_cout),
    .\SAÍDA (in_4[28]), .DIREITA(A[29]));  // open: SET, DIREITA_A, COMPARADOR
  celULA celula_5 (
    .cout(celula_5_cout), .ESQUERDA(A[26]), .\OPERAÇÃO (in_3), .A(A[27]), .B(B[27]), .cin(celula_4_cout),
    .\SAÍDA (in_4[27]), .DIREITA(A[28]));  // open: SET, DIREITA_A, COMPARADOR
  celULA celula_6 (
    .cout(celula_6_cout), .ESQUERDA(A[25]), .\OPERAÇÃO (in_3), .A(A[26]), .B(B[26]), .cin(celula_5_cout),
    .\SAÍDA (in_4[26]), .DIREITA(A[27]));  // open: SET, DIREITA_A, COMPARADOR
  celULA celula_7 (
    .cout(celula_7_cout), .ESQUERDA(A[24]), .\OPERAÇÃO (in_3), .A(A[25]), .B(B[25]), .cin(celula_6_cout),
    .\SAÍDA (in_4[25]), .DIREITA(A[26]));  // open: SET, DIREITA_A, COMPARADOR
  celULA celula_8 (
    .cout(celula_8_cout), .ESQUERDA(A[23]), .\OPERAÇÃO (in_3), .A(A[24]), .B(B[24]), .cin(celula_7_cout),
    .\SAÍDA (in_4[24]), .DIREITA(A[25]));  // open: SET, DIREITA_A, COMPARADOR
  celULA celula_9 (
    .cout(celula_9_cout), .ESQUERDA(A[22]), .\OPERAÇÃO (in_3), .A(A[23]), .B(B[23]), .cin(celula_8_cout),
    .\SAÍDA (in_4[23]), .DIREITA(A[24]));  // open: SET, DIREITA_A, COMPARADOR
  celULA celula_10 (
    .cout(celula_10_cout), .ESQUERDA(A[21]), .\OPERAÇÃO (in_3), .A(A[22]), .B(B[22]), .cin(celula_9_cout),
    .\SAÍDA (in_4[22]), .DIREITA(A[23]));  // open: SET, DIREITA_A, COMPARADOR
  celULA celula_11 (
    .cout(celula_11_cout), .ESQUERDA(A[20]), .\OPERAÇÃO (in_3), .A(A[21]), .B(B[21]), .cin(celula_10_cout),
    .\SAÍDA (in_4[21]), .DIREITA(A[22]));  // open: SET, DIREITA_A, COMPARADOR
  celULA celula_12 (
    .cout(celula_12_cout), .ESQUERDA(A[19]), .\OPERAÇÃO (in_3), .A(A[20]), .B(B[20]), .cin(celula_11_cout),
    .\SAÍDA (in_4[20]), .DIREITA(A[21]));  // open: SET, DIREITA_A, COMPARADOR
  celULA celula_13 (
    .cout(celula_13_cout), .ESQUERDA(A[18]), .\OPERAÇÃO (in_3), .A(A[19]), .B(B[19]), .cin(celula_12_cout),
    .\SAÍDA (in_4[19]), .DIREITA(A[20]));  // open: SET, DIREITA_A, COMPARADOR
  celULA celula_14 (
    .cout(celula_14_cout), .ESQUERDA(A[17]), .\OPERAÇÃO (in_3), .A(A[18]), .B(B[18]), .cin(celula_13_cout),
    .\SAÍDA (in_4[18]), .DIREITA(A[19]));  // open: SET, DIREITA_A, COMPARADOR
  celULA celula_15 (
    .cout(celula_15_cout), .ESQUERDA(A[16]), .\OPERAÇÃO (in_3), .A(A[17]), .B(B[17]), .cin(celula_14_cout),
    .\SAÍDA (in_4[17]), .DIREITA(A[18]));  // open: SET, DIREITA_A, COMPARADOR
  celULA celula_16 (
    .cout(celula_16_cout), .ESQUERDA(A[15]), .\OPERAÇÃO (in_3), .A(A[16]), .B(B[16]), .cin(celula_15_cout),
    .\SAÍDA (in_4[16]), .DIREITA(A[17]));  // open: SET, DIREITA_A, COMPARADOR
  celULA celula_17 (
    .cout(celula_17_cout), .ESQUERDA(A[14]), .\OPERAÇÃO (in_3), .A(A[15]), .B(B[15]), .cin(celula_16_cout),
    .\SAÍDA (in_4[15]), .DIREITA(A[16]));  // open: SET, DIREITA_A, COMPARADOR
  celULA celula_18 (
    .cout(celula_18_cout), .ESQUERDA(A[13]), .\OPERAÇÃO (in_3), .A(A[14]), .B(B[14]), .cin(celula_17_cout),
    .\SAÍDA (in_4[14]), .DIREITA(A[15]));  // open: SET, DIREITA_A, COMPARADOR
  celULA celula_19 (
    .cout(celula_19_cout), .ESQUERDA(A[12]), .\OPERAÇÃO (in_3), .A(A[13]), .B(B[13]), .cin(celula_18_cout),
    .\SAÍDA (in_4[13]), .DIREITA(A[14]));  // open: SET, DIREITA_A, COMPARADOR
  celULA celula_20 (
    .cout(celula_20_cout), .ESQUERDA(A[11]), .\OPERAÇÃO (in_3), .A(A[12]), .B(B[12]), .cin(celula_19_cout),
    .\SAÍDA (in_4[12]), .DIREITA(A[13]));  // open: SET, DIREITA_A, COMPARADOR
  celULA celula_21 (
    .cout(celula_21_cout), .ESQUERDA(A[10]), .\OPERAÇÃO (in_3), .A(A[11]), .B(B[11]), .cin(celula_20_cout),
    .\SAÍDA (in_4[11]), .DIREITA(A[12]));  // open: SET, DIREITA_A, COMPARADOR
  celULA celula_22 (
    .cout(celula_22_cout), .ESQUERDA(A[9]), .\OPERAÇÃO (in_3), .A(A[10]), .B(B[10]), .cin(celula_21_cout),
    .\SAÍDA (in_4[10]), .DIREITA(A[11]));  // open: SET, DIREITA_A, COMPARADOR
  celULA celula_23 (
    .cout(celula_23_cout), .ESQUERDA(A[8]), .\OPERAÇÃO (in_3), .A(A[9]), .B(B[9]), .cin(celula_22_cout),
    .\SAÍDA (in_4[9]), .DIREITA(A[10]));  // open: SET, DIREITA_A, COMPARADOR
  celULA celula_24 (
    .cout(celula_24_cout), .ESQUERDA(A[7]), .\OPERAÇÃO (in_3), .A(A[8]), .B(B[8]), .cin(celula_23_cout),
    .\SAÍDA (in_4[8]), .DIREITA(A[9]));  // open: SET, DIREITA_A, COMPARADOR
  celULA celula_25 (
    .cout(celula_25_cout), .ESQUERDA(A[6]), .\OPERAÇÃO (in_3), .A(A[7]), .B(B[7]), .cin(celula_24_cout),
    .\SAÍDA (in_4[7]), .DIREITA(A[8]));  // open: SET, DIREITA_A, COMPARADOR
  celULA celula_26 (
    .cout(celula_26_cout), .ESQUERDA(A[5]), .\OPERAÇÃO (in_3), .A(A[6]), .B(B[6]), .cin(celula_25_cout),
    .\SAÍDA (in_4[6]), .DIREITA(A[7]));  // open: SET, DIREITA_A, COMPARADOR
  celULA celula_27 (
    .cout(celula_27_cout), .ESQUERDA(A[4]), .\OPERAÇÃO (in_3), .A(A[5]), .B(B[5]), .cin(celula_26_cout),
    .\SAÍDA (in_4[5]), .DIREITA(A[6]));  // open: SET, DIREITA_A, COMPARADOR
  celULA celula_28 (
    .cout(celula_28_cout), .ESQUERDA(A[3]), .\OPERAÇÃO (in_3), .A(A[4]), .B(B[4]), .cin(celula_27_cout),
    .\SAÍDA (in_4[4]), .DIREITA(A[5]));  // open: SET, DIREITA_A, COMPARADOR
  celULA celula_29 (
    .cout(celula_29_cout), .ESQUERDA(A[2]), .\OPERAÇÃO (in_3), .A(A[3]), .B(B[3]), .cin(celula_28_cout),
    .\SAÍDA (in_4[3]), .DIREITA(A[4]));  // open: SET, DIREITA_A, COMPARADOR
  celULA celula_30 (
    .cout(celula_30_cout), .ESQUERDA(B[1]), .\OPERAÇÃO (in_3), .A(A[2]), .B(B[2]), .cin(celula_29_cout),
    .\SAÍDA (in_4[2]), .DIREITA(A[3]));  // open: SET, DIREITA_A, COMPARADOR
  celULA celula_31 (
    .cout(celula_31_cout), .ESQUERDA(A[0]), .\OPERAÇÃO (in_3), .A(B[1]), .B(A[1]), .cin(celula_30_cout),
    .\SAÍDA (in_4[1]), .DIREITA(A[2]));  // open: SET, DIREITA_A, COMPARADOR
  celULA celula_32 (
    .cout(celula_32_cout), .ESQUERDA(celula_32_cout), .\OPERAÇÃO (in_3), .A(B[0]), .B(A[0]),
    .cin(celula_31_cout), .\SAÍDA (in_4[0]), .DIREITA(B[1]));  // open: SET, DIREITA_A, COMPARADOR
  and and_1 (out_6, ~in_4[0], ~in_4[1], ~in_4[2], ~in_4[3], ~in_4[4], ~in_4[5], ~in_4[6], ~in_4[7], ~in_4[8], ~in_4[9], ~in_4[10], ~in_4[11], ~in_4[12], ~in_4[13], ~in_4[14], ~in_4[15], ~in_4[16], ~in_4[17], ~in_4[18], ~in_4[19], ~in_4[20], ~in_4[21], ~in_4[22], ~in_4[23], ~in_4[24], ~in_4[25], ~in_4[26], ~in_4[27], ~in_4[28], ~in_4[29], ~in_4[30], ~in_4[31]);  // AND_Gate
  // also tied to GND on the sheet: celula_32_cout
endmodule

module OVERFLOW (
  input  E1,
  input  E2,
  input  \SAÍDA ,
  input  in_4,
  input  in_5,
  input  in_6,
  input  [4:0] OP,
  output OVERFLOW
);

  wire and_1_out, and_2_out, and_3_out, and_4_out, and_5_out, and_6_out, and_7_out, and_8_out, and_9_out,
       and_10_out, or_1_out;

  and and_1 (and_1_out, ~E1, ~E2, \SAÍDA );  // AND_Gate
  and and_2 (and_2_out, E1, E2, ~\SAÍDA );  // AND_Gate
  or or_1 (or_1_out, and_1_out, and_2_out);
  and and_3 (and_3_out, ~OP[4], ~OP[3], OP[2], OP[1], ~OP[0]);  // AND_Gate
  and and_4 (and_4_out, ~OP[4], ~OP[3], OP[2], OP[1], OP[0]);  // AND_Gate
  and and_5 (and_5_out, ~OP[4], OP[3], ~OP[2], ~OP[1], ~OP[0]);  // AND_Gate
  and and_6 (and_6_out, ~OP[4], OP[3], ~OP[2], ~OP[1], OP[0]);  // AND_Gate
  and and_7 (and_7_out, or_1_out, and_3_out);
  and and_8 (and_8_out, and_4_out, in_4);
  and and_9 (and_9_out, and_5_out, in_5);
  and and_10 (and_10_out, and_6_out, in_6);
  Multiplexer #(.select(2), .enable("false")) multiplexer_1 (
    .in0(and_9_out), .in1(and_10_out), .in2(and_7_out), .in3(and_8_out), .out(OVERFLOW), .sel(OP[1:0]));
endmodule
